# Fritzing sketch garageController (saved by Fritzing 0.9.6b)
circuit board: 10cm x 7.66077cm
breadboards: 1

parts:
  Q1 = NPN-Transistor [package="TO92 [THT]"]
  Q2 = NPN-Transistor [package="TO92 [THT]"]
  Relais_Siren = songle relay
  Q3 = NPN-Transistor [package="TO92 [THT]"]
  -12V_Light_+ = Screw terminal - 2 pins [package=THT]
  Reedswitch = Screw terminal - 2 pins [package=THT]
  +12V_IN- = Screw terminal - 2 pins [package=THT]
  Magnet_I = Screw terminal - 2 pins [package=THT]
  Magnet_II = Screw terminal - 2 pins [package=THT]
  -Siren+ = Screw terminal - 2 pins [package=THT]
  +LED_Door- = Screw terminal - 2 pins [package=THT]
  Relais_Magnet = songle relay
  Buttonsignal_Door = Screw terminal - 2 pins [package=THT]
  10k = Resistor [tolerance=±5% power=0.25 resistance=10000 package=THT]
  1k = Resistor [tolerance=±5% power=0.25 resistance=1000 package=THT]
  1k_2 = Resistor [tolerance=±5% power=0.25 resistance=1000 package=THT]
  1k_3 = Resistor [tolerance=±5% power=0.25 resistance=1000 package=THT]
  10k_2 = Resistor [tolerance=±5% power=0.25 resistance=10000 package=THT]
  100 = Resistor [tolerance=±5% resistance=100 power=0.25 package=THT]
  100_2 = Resistor [tolerance=±5% resistance=100 power=0.25 package=THT]
  100_3 = Resistor [tolerance=±5% resistance=100 power=0.25 package=THT]
  D3 = Rectifier Diode [part_number=1N4001 package="300 mil [THT]"]
  D2 = Rectifier Diode [part_number=1N4001 package="300 mil [THT]"]
  D4 = Rectifier Diode [part_number=1N4001 package="300 mil [THT]"]
  Relais_Light = songle relay
  SW_Main = Header 2 [package=molex-1x2_lock]
  SW_Mode = Header 2 [package=molex-1x2_lock]
  LED_red = Header 2 [package=molex-1x2_lock]
  SW_Light = Header 2 [package=molex-1x2_lock]
  LED_grn = Header 2 [package=molex-1x2_lock]
  J1 = male pin header, 5 pins [form="♂ (male)"]
  Pro_Mini = Arduino Pro Mini v13
  10k_3 = Resistor [tolerance=±5% power=0.25 resistance=10000 package=THT]
  D11 = Header 2 [package=molex-1x2_lock]
  A0 = Header 2 [package=molex-1x2_lock]
  J2 = male pin header, 2 pins [form="♂ (male)"]
  J3 = male pin header, 2 pins [form="♂ (male)"]
  J4 = male pin header, 2 pins [form="♂ (male)"]

nets (from the pcb view):
  N1: Q1.E, Q2.E, Q3.E, -12V_Light_+.pin2, +12V_IN-.pin2, Magnet_I.pin2, Magnet_II.pin1, -Siren+.pin2, 10k.Pin_0, 10k_2.Pin_0, 100.Pin_1, 100_2.Pin_1, 100_3.Pin_1, J1.pin4, Pro_Mini.GND, 10k_3.Pin_0, D11.1, A0.2, J3.pin1, J3.pin2
  N2: Q1.B, 1k.Pin_0
  N3: Q1.C, Relais_Magnet.GND, D2.anode
  N4: Q2.B, 1k_2.Pin_0
  N5: Q2.C, Relais_Siren.GND, D3.anode
  VCC: Relais_Siren.VCC, Reedswitch.pin2, Relais_Magnet.VCC, Buttonsignal_Door.pin2, D3.cathode, D2.cathode, D4.cathode, Relais_Light.VCC, SW_Mode.1, SW_Light.1, J1.pin3, Pro_Mini.VCC, J4.pin1, J4.pin2
  N6: Relais_Siren.NO, -Siren+.pin1
  N7: Relais_Siren.COMMON, Relais_Magnet.COMMON, Relais_Light.COMMON, SW_Main.2, Pro_Mini.RAW, J2.pin1, J2.pin2
  N8: Q3.B, 1k_3.Pin_0
  N9: Q3.C, D4.anode, Relais_Light.GND
  N10: -12V_Light_+.pin1, Relais_Light.NO
  N11: Reedswitch.pin1, 10k.Pin_1, Pro_Mini.D12/MISO
  N12: +12V_IN-.pin1, SW_Main.1
  N13: Magnet_I.pin1, Magnet_II.pin2, Relais_Magnet.NO
  N14: +LED_Door-.pin1, 100_3.Pin_0
  N15: +LED_Door-.pin2, Pro_Mini.D6_PWM
  N16: Buttonsignal_Door.pin1, Pro_Mini.D5_PWM, 10k_3.Pin_1
  N17: 1k.Pin_1, Pro_Mini.D9_PWM
  N18: 1k_2.Pin_1, Pro_Mini.D8
  N19: 1k_3.Pin_1, Pro_Mini.D7
  N20: 10k_2.Pin_1, SW_Mode.2, Pro_Mini.D11_PWM/MOSI
  N21: 100.Pin_0, LED_red.1
  N22: 100_2.Pin_0, LED_grn.1
  N23: LED_red.2, Pro_Mini.D4
  N24: SW_Light.2, Pro_Mini.D2
  N25: LED_grn.2, Pro_Mini.D3_PWM
  N26: J1.pin1, Pro_Mini.D0/TX
  N27: J1.pin2, Pro_Mini.D1/RX
  N28: J1.pin5, Pro_Mini.RESET
  N29: Pro_Mini.A0, A0.1
  N30: Pro_Mini.D10_PWM/SS, D11.2

notes:
  MerchmanProductions 2021
  -
  RST GND VCC RXI TXO
  GND
  5V     GND    12V
